# Fritzing sketch Scale (saved by Fritzing 0.9.3b)

parts:
  ESP8266 = NodeMCU V1.0
  SSD1306 = Grove OLED 128x96
  HX711 = HX711 Weighing Sensor Module

nets:
  N1: ESP8266.D1, SSD1306.SCL
  N2: ESP8266.D2, SSD1306.SDA
  N3: ESP8266.D3, HX711.CK/TX
  N4: ESP8266.D8, HX711.DO/RX
  GND: ESP8266.GND, SSD1306.GND, HX711.GND
  VCC: ESP8266.3V3, SSD1306.VCC, HX711.VCC

custom parts:
  NodeMCU V1.0: ESP8266 based NodeMCU
